// Digital circuit main.dig as structural Verilog
module main (
  input  u2,
  input  u3,
  input  u5,
  input  u1,
  input  clk,
  input  in_10,
  output right,
  output left,
  output up,
  output down,
  output \end 
);

  wire and_1_out, and_2_out, and_3_out, and_4_out, and_5_out, and_6_out, and_7_out, and_8_out, and_9_out,
       and_10_out, and_11_out, decoder_1_out_0, decoder_1_out_1, decoder_1_out_2, decoder_1_out_3,
       decoder_1_out_5, decoder_1_out_6, decoder_1_out_7, decoder_1_out_8, main_logic_1_not_u1_plus_u2u5,
       main_logic_1_not_u2, main_logic_1_not_u3, main_logic_1_u1not_u5, main_logic_1_u2_2, main_logic_1_u2u3,
       main_logic_1_u3_2, main_logic_1_u5_u1_plus_u2, or_1_out, or_2_out, or_3_out, or_4_out, or_5_out,
       or_6_out, or_7_out, or_8_out, switchdt_1_p3;
  wire [3:0] D4_q, \Замкнуть_после_выбора_режима_p3 ;

  main_logic main_logic_1 (
    .U1(u1), .U2(u2), .U3(u3), .U5(u5), .u5_u1_plus_u2(main_logic_1_u5_u1_plus_u2),
    .not_u1_plus_u2u5(main_logic_1_not_u1_plus_u2u5), .u3_2(main_logic_1_u3_2), .not_u3(main_logic_1_not_u3),
    .u2_2(main_logic_1_u2_2), .u1not_u5(main_logic_1_u1not_u5), .not_u2(main_logic_1_not_u2),
    .u2u3(main_logic_1_u2u3));
  or or_1 (or_1_out, main_logic_1_u5_u1_plus_u2, main_logic_1_u1not_u5);
  and and_1 (and_1_out, decoder_1_out_0, main_logic_1_not_u1_plus_u2u5);
  or or_2 (or_2_out, or_8_out, and_1_out);
  D_FF D4 (.D(or_2_out), .C(switchdt_1_p3), .Q(D4_q[3]));  // open: nQ
  and and_2 (and_2_out, decoder_1_out_0, main_logic_1_u1not_u5);
  and and_3 (and_3_out, or_6_out, main_logic_1_not_u2);
  and and_4 (and_4_out, main_logic_1_u1not_u5, decoder_1_out_0);
  or or_3 (or_3_out, and_2_out, and_3_out, or_7_out);
  D_FF D3 (.D(or_3_out), .C(switchdt_1_p3), .Q(D4_q[2]));  // open: nQ
  and and_5 (and_5_out, down, main_logic_1_u2u3);
  and and_6 (and_6_out, or_7_out, main_logic_1_not_u3);
  // SwitchDT switchdt_1: pin names not known; wires that end beside it: in_10, clk, switchdt_1_p3
  and and_7 (and_7_out, or_7_out, main_logic_1_not_u3);
  or or_4 (or_4_out, and_7_out, and_6_out, and_4_out);
  D_FF D2 (.D(or_4_out), .C(switchdt_1_p3), .Q(D4_q[1]));  // open: nQ
  and and_8 (and_8_out, down, main_logic_1_not_u2);
  and and_9 (and_9_out, decoder_1_out_1, main_logic_1_not_u2);
  Decoder #(.Selector_Bits(4)) decoder_1 (
    .sel(\Замкнуть_после_выбора_режима_p3 ), .out_0(decoder_1_out_0), .out_1(decoder_1_out_1),
    .out_2(decoder_1_out_2), .out_3(decoder_1_out_3), .out_4(down), .out_5(decoder_1_out_5),
    .out_6(decoder_1_out_6), .out_7(decoder_1_out_7), .out_8(decoder_1_out_8), .out_9(\end ));  // open: out_10, out_11, out_12, out_13, out_14, out_15
  // SwitchDT #(.Bits(4)) Замкнуть_после_выбора_режима: pin names not known; wires that end beside it: 4'b0000, D4_q, \Замкнуть_после_выбора_режима_p3 , decoder_1_out_2
  and and_10 (and_10_out, decoder_1_out_1, main_logic_1_u2u3);
  or or_5 (or_5_out, and_11_out, and_10_out, and_9_out, or_8_out, and_5_out, and_8_out);
  D_FF D1 (.D(or_5_out), .C(switchdt_1_p3), .Q(D4_q[0]));  // open: nQ
  and and_11 (and_11_out, decoder_1_out_0, or_1_out);
  or or_6 (or_6_out, decoder_1_out_1, down);
  or or_7 (or_7_out, decoder_1_out_3, decoder_1_out_7);
  or or_8 (or_8_out, decoder_1_out_5, decoder_1_out_6, decoder_1_out_8, \end );
  or or_9 (right, decoder_1_out_1, decoder_1_out_7);
  or or_10 (left, decoder_1_out_2, decoder_1_out_5, decoder_1_out_6);
  or or_11 (up, decoder_1_out_3, decoder_1_out_5, decoder_1_out_7, decoder_1_out_8);
endmodule
