// Digital circuit main_logic.dig as structural Verilog
module main_logic (
  input  U1,
  input  U2,
  input  U3,
  input  U5,
  output u5_u1_plus_u2,
  output not_u1_plus_u2u5,
  output u3_2,
  output not_u3,
  output u2_2,
  output u1not_u5,
  output not_u2,
  output u2u3
);

  wire and_1_out, or_1_out, or_2_out;

  or or_1 (or_1_out, U1, U2);
  and and_1 (and_1_out, U2, U5);
  and and_2 (u5_u1_plus_u2, U5, or_1_out);
  or or_2 (or_2_out, U1, and_1_out);
  and and_3 (u1not_u5, U1, ~U5);  // And
  not not_1 (not_u3, U3);
  not not_2 (not_u2, U2);
  and and_4 (u2u3, U2, U3);
  not not_3 (not_u1_plus_u2u5, or_2_out);

  assign u2_2 = U2;
  assign u3_2 = U3;
endmodule
